// Logisim project index.circ as structural Verilog
module HA (
  input  A,
  input  B,
  output sum,
  output carry
);

  xor xor_1 (sum, A, B);
  and and_1 (carry, A, B);
endmodule

module FullAdder (
  input  Cin,
  input  A,
  input  B,
  output Sum,
  output Cout
);

  wire ha_1_carry, ha_1_sum, ha_2_carry;

  HA ha_1 (.A(A), .B(B), .sum(ha_1_sum), .carry(ha_1_carry));
  HA ha_2 (.A(Cin), .B(ha_1_sum), .sum(Sum), .carry(ha_2_carry));
  xor xor_1 (Cout, ha_2_carry, ha_1_carry);
endmodule

module _5_bitAdder (
  input  B0,
  input  A0,
  input  B1,
  input  A1,
  input  B2,
  input  A2,
  input  B3,
  input  A3,
  input  B4,
  input  A4,
  input  Cin,
  output carry,
  output S3,
  output S2,
  output S1,
  output S0,
  output S4
);

  wire fulladder_2_cout, fulladder_3_cout, fulladder_4_cout, fulladder_5_cout;

  FullAdder fulladder_1 (.Cin(fulladder_2_cout), .A(A4), .B(B4), .Sum(S4), .Cout(carry));
  FullAdder fulladder_2 (.Cin(fulladder_3_cout), .A(A3), .B(B3), .Sum(S3), .Cout(fulladder_2_cout));
  FullAdder fulladder_3 (.Cin(fulladder_4_cout), .A(A2), .B(B2), .Sum(S2), .Cout(fulladder_3_cout));
  FullAdder fulladder_4 (.Cin(fulladder_5_cout), .A(A1), .B(B1), .Sum(S1), .Cout(fulladder_4_cout));
  FullAdder fulladder_5 (.Cin(Cin), .A(A0), .B(B0), .Sum(S0), .Cout(fulladder_5_cout));
endmodule
